# Fritzing sketch PCB (saved by Fritzing 0.9.5d)
circuit board: 11.9145cm x 14.7719cm

parts:
  Unlock_Relay = songle relay
  Unlock_Res = Resistor [tolerance=±5% resistance=1k package=THT]
  XTAL1 = Crystal [frequency="16 Mhz" package=THT]
  Unlock_NPN = NPN-Transistor [package="TO92 [THT]"]
  Unlock_Diode = Rectifier Diode [part_number=1N4001 package="300 mil [THT]"]
  Lock_Relay = songle relay
  Lock_Res = Resistor [tolerance=±5% resistance=1k package=THT]
  Lock_NPN = NPN-Transistor [package="TO92 [THT]"]
  Lock_Diode = Rectifier Diode [part_number=1N4001 package="300 mil [THT]"]
  AngelEyes_Relay = songle relay
  AngelEyes_Res = Resistor [tolerance=±5% resistance=1k package=THT]
  AngelEyes_NPN = NPN-Transistor [package="TO92 [THT]"]
  AngelEyes_Diode = Rectifier Diode [part_number=1N4001 package="300 mil [THT]"]
  Starter_Relay = songle relay
  Starter_Res = Resistor [tolerance=±5% resistance=1k package=THT]
  Starter_NPN = NPN-Transistor [package="TO92 [THT]"]
  Starter_Diode = Rectifier Diode [part_number=1N4001 package="300 mil [THT]"]
  Ignition_Relay = songle relay
  Ignition_Res = Resistor [tolerance=±5% resistance=1k package=THT]
  Ignition_NPN = NPN-Transistor [package="TO92 [THT]"]
  Ignition_Diode = Rectifier Diode [part_number=1N4001 package="300 mil [THT]"]
  Warning_Lights_Relay = songle relay
  Warning_Lights_Res = Resistor [tolerance=±5% resistance=1k package=THT]
  Warning_Lights_NPN = NPN-Transistor [package="TO92 [THT]"]
  Warning_Lights_Diode = Rectifier Diode [part_number=1N4001 package="300 mil [THT]"]
  Additional_Relay = songle relay
  Additional_Res = Resistor [tolerance=±5% resistance=1k package=THT]
  Additional_NPN = NPN-Transistor [package="TO92 [THT]"]
  Additional_Diode = Rectifier Diode [part_number=1N4001 package="300 mil [THT]"]
  U1 = atmega168 [package=dip]
  U2 = Voltage Regulator - 5V [package="TO220 [THT]"]
  5V_out_cap = Ceramic Capacitor [capacitance=10µF voltage=50V package="100 mil [THT, multilayer]"]
  12V_in_cap = Ceramic Capacitor [capacitance=0.33µF voltage=50V package="100 mil [THT, multilayer]"]
  CLK_cap1 = Ceramic Capacitor [capacitance=22pF voltage=50V package="100 mil [THT, multilayer]"]
  CLK_cap2 = Ceramic Capacitor [capacitance=22pF voltage=50V package="100 mil [THT, multilayer]"]
  Composant1 = Bluetooth HC-05 Macho
  R2 = Resistor [tolerance=±5% resistance=10k package=THT]
  R3 = Resistor [tolerance=±5% resistance=100k package=THT]

nets:
  VCC: Unlock_Relay.VCC, Unlock_Diode.cathode, Lock_Relay.VCC, Lock_Diode.cathode, AngelEyes_Relay.VCC, AngelEyes_Diode.cathode, Starter_Relay.VCC, Starter_Diode.cathode, Ignition_Relay.VCC, Ignition_Diode.cathode, Warning_Lights_Relay.VCC, Warning_Lights_Diode.cathode, Additional_Relay.VCC, Additional_Diode.cathode, U1.VCC, U1.AVCC, U1.AREF, U2.output_voltage, 5V_out_cap.1, Composant1.VCC
  N1: Unlock_Relay.GND, Unlock_NPN.C, Unlock_Diode.anode
  N2: Unlock_Res.Pin_0, Unlock_NPN.B
  N3: Unlock_Res.Pin_1, U1.D13
  N4: XTAL1.pin_0, U1.XLAT2, CLK_cap2.0
  N5: XTAL1.pin_1, U1.XLAT1, CLK_cap1.1
  GND: Unlock_NPN.E, Lock_NPN.E, AngelEyes_NPN.E, Starter_NPN.E, Ignition_NPN.E, Warning_Lights_NPN.E, Additional_NPN.E, U1.GND, U2.GND, 5V_out_cap.0, 12V_in_cap.1, CLK_cap1.0, CLK_cap2.1, Composant1.GND, R2.Pin_1
  N6: Lock_Relay.GND, Lock_NPN.C, Lock_Diode.anode
  N7: Lock_Res.Pin_0, Lock_NPN.B
  N8: Lock_Res.Pin_1, U1.D12
  N9: AngelEyes_Relay.GND, AngelEyes_NPN.C, AngelEyes_Diode.anode
  N10: AngelEyes_Res.Pin_0, AngelEyes_NPN.B
  N11: AngelEyes_Res.Pin_1, U1.D11_(PWM)
  N12: Starter_Relay.GND, Starter_NPN.C, Starter_Diode.anode
  N13: Starter_Res.Pin_0, Starter_NPN.B
  N14: Starter_Res.Pin_1, U1.D10_(PWM)
  N15: Ignition_Relay.GND, Ignition_NPN.C, Ignition_Diode.anode
  N16: Ignition_Res.Pin_0, Ignition_NPN.B
  N17: Ignition_Res.Pin_1, U1.D9_(PWM)
  N18: Warning_Lights_Relay.GND, Warning_Lights_NPN.C, Warning_Lights_Diode.anode
  N19: Warning_Lights_Res.Pin_0, Warning_Lights_NPN.B
  N20: Warning_Lights_Res.Pin_1, U1.D8
  N21: Additional_Relay.GND, Additional_NPN.C, Additional_Diode.anode
  N22: Additional_Res.Pin_0, Additional_NPN.B
  N23: Additional_Res.Pin_1, U1.D7
  N24: U1.D2, Composant1.TXD
  N25: U1.D3_(PWM), Composant1.RXD
  N26: U1.A5, R2.Pin_0, R3.Pin_0
  N27: U2.input_voltage, 12V_in_cap.0, R3.Pin_1

notes:
  HABIBI CORP.
  https://pimpmyhabibi.ddns.net
